# Fritzing sketch CoreElectronicsGroup1FinalPCB (saved by Fritzing 0.9.3b)
circuit board: 13.3cm x 9.6cm
breadboards: 2

parts:
  Geiger1 = RJ11 Jack [package=rj11-6]
  Geiger2 = RJ11 Jack [package=rj11-6]
  IMU = 9-DOF Absolute Orientation IMU Fusion Breakout - BNO055
  50k = Resistor [tolerance=±5% resistance=50k package=THT]
  50k_2 = Resistor [tolerance=±5% resistance=50k package=THT]
  Feather_M0 = Adafruit Feather M0 Adalogger [part_number="Adafruit #2796"]
  J1 = female pin header, 16 pins [form="♀ (female)"]
  J2 = female pin header, 12 pins [form="♀ (female)"]
  J3 = screw terminal, 2 pins
  J4 = screw terminal, 2 pins
  J5 = screw terminal, 2 pins
  J6 = screw terminal, 2 pins
  J7 = screw terminal, 2 pins
  J8 = screw terminal, 2 pins
  J9 = screw terminal, 2 pins
  J10 = screw terminal, 2 pins
  J11 = screw terminal, 2 pins
  J12 = screw terminal, 2 pins
  5V3V3 = female pin header, 4 pins [form="♀ (female)"]
  J13 = female pin header, 16 pins [form="♀ (female)"]
  J14 = female pin header, 12 pins [form="♀ (female)"]  # not connected
  J15 = female pin header, 1 pin [form="♀ (female)"]
  J16 = female pin header, 10 pins [form="♀ (female)"]
  J17 = rounded female pin header, 10 pins [form="♀ (female rounded)"]

nets:
  N1: Geiger1.2, Geiger2.2, 50k.Pin_1, 50k_2.Pin_1
  N2: Geiger1.3, Feather_M0.D11, J2.pin6
  N3: Geiger1.4, Geiger2.4, IMU.5.0V, 50k_2.Pin_0, J4.pin2, J6.pin2, J9.pin2, J11.pin2, 5V3V3.pin3, J13.pin15, J17.pin8, J17.pin10
  GND: Geiger1.5, Geiger2.5, IMU.GND, 50k.Pin_0, Feather_M0.GND, J1.pin4, J1.pin16, J3.pin1, J4.pin1, J6.pin1, J9.pin1, J11.pin1, 5V3V3.pin4, J13.pin13, J17.pin3, J17.pin9
  N4: Geiger2.3, Feather_M0.D12, J2.pin5
  N5: IMU.SDA_5V, Feather_M0.SDA, J2.pin12, J5.pin2, J7.pin2, J10.pin2, J12.pin2
  N6: IMU.SCL_5V, Feather_M0.SCL, J2.pin11, J5.pin1, J7.pin1, J10.pin1, J12.pin1
  N7: Feather_M0.D1, J1.pin15, J16.pin7
  N8: Feather_M0.D0, J1.pin14, J16.pin3
  N9: Feather_M0.MISO, J1.pin13
  N10: Feather_M0.MOSI, J1.pin12
  N11: Feather_M0.SCK, J1.pin11
  N12: Feather_M0.A5, J1.pin10
  N13: Feather_M0.A4, J1.pin9
  N14: Feather_M0.A3, J1.pin8
  N15: Feather_M0.A2, J1.pin7
  N16: Feather_M0.A1, J1.pin6
  N17: Feather_M0.A0, J1.pin5
  N18: Feather_M0.AREF, J1.pin3
  N19: Feather_M0.+3V3, J1.pin2
  N20: Feather_M0.!RESET, J1.pin1
  N21: Feather_M0.VBAT, J2.pin1
  N22: Feather_M0.EN, J2.pin2
  N23: Feather_M0.VBUS, J2.pin3
  N24: Feather_M0.D13, J2.pin4
  N25: Feather_M0.D10, J2.pin7
  N26: Feather_M0.D9, J2.pin8
  N27: Feather_M0.D6, J2.pin9
  N28: Feather_M0.D5, J2.pin10
  N29: J3.pin2, 5V3V3.pin1, 5V3V3.pin2
  N30: J8.pin1, J15.pin1

notes:
  RMC PH549
  Eye of the
  Geiger
  GPS
  Relay
  L2SCL
  L2SDA
  GND
  3V3
  L1SCL
  L1SDA
  CUTOFF
  PrSCL
  PrSDA
  L3SDA
  L3SCL
  5VIN
  LM3671

custom parts:
  9-DOF Absolute Orientation IMU Fusion Breakout - BNO055: A MEMS accelerometer, magnetometer and gyroscope on a single die with a high speed ARM Cortex-M0 based processor to digest all the sensor data, abstract the sensor fusion and real time requirements away, and spit out data you can use in quaternions, Euler angles or vectors.
  Adafruit Feather M0 Adalogger: This is the Adafruit Feather M0 Adalogger - our take on an 'all-in-one' Cortex M0 datalogger (or data-reader) with built in USB and battery charging. Its an Adafruit Feather M0 with a microSD holder ready to rock! We have other boards in the Feather family, check'em out here At the Feather M0's heart is an ATSAMD21G18 ARM Cortex M0 processor, clocked at 48 MHz and at 3.3V logic, the same one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
